# Fritzing sketch IrrigationStationHardware (saved by Fritzing 0.9.4)

parts:
  Part1 = Arduino Mega 2560 (Rev3)
  DoIt_ESP-13_WifiShield = WeMos D1 Mini
  M1 = DC Motor
  L298N1 = L298N DC motor driver
  Part2 = Soil Moisture Sensor
  S1 = Momentary Switch [package=ksa_sealed_tac_switch]
  S2 = Momentary Switch [package=ksa_sealed_tac_switch]
  U1 = 74HC595 SMD [package="SO16 [SMD]"]
  U2 = 74HC595 SMD [package="SO16 [SMD]"]

nets:
  N1: Part1.A0, Part2.SIG
  N2: Part1.D19/RX1, DoIt_ESP-13_WifiShield.TX
  N3: Part1.D18/TX1, DoIt_ESP-13_WifiShield.RX
  N4: Part1.AREF, DoIt_ESP-13_WifiShield.3V3
  GND: Part1.GND, DoIt_ESP-13_WifiShield.G, L298N1.GND, L298N1.IN3, Part2.GND, S1.3, S2.3, U1.GND, U2.GND
  N5: Part1.D9_PWM, U1.DS
  N6: Part1.D8_PWM, U1.SH_CP
  3V3: Part1.3V3, Part2.VCC
  VCC: Part1.5V, L298N1.IN4, U1.VCC, U2.VCC
  VIN: Part1.VIN, L298N1.12V
  N7: Part1.D2_PWM, S2.2
  N8: Part1.D3_PWM, S1.2
  N9: Part1.D6_PWM, L298N1.ENB
  N10: Part1.D7_PWM, U1.ST_CP
  N11: M1.pin_1, L298N1.OUT4
  N12: M1.pin_2, L298N1.OUT3
  N13: U1.Q7', U2.DS

custom parts:
  L298N DC motor driver: 2x DC motor driver with 78M05 positive voltage regulator (7..35 V) L298N: max 46 V, 2 A Set 5 V Enable jumper to enable 5 V regultor (needed for the L298N) and +5 V output at screw terminal or supply external +5 V at screw terminal Set ENA and/or ENB to +5 V to enable motor permanently or supply ENA and/or ENB with PWM signal IN1 and IN2 set rotation directory for motor A (OUT1/OUT2) IN2 and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
